// Logisim project D_FF_Async.circ as structural Verilog
module main (
  input  D,
  input  CLK,
  input  set,
  input  clr,
  input  in_5,
  input  in_6,
  input  in_7,
  input  in_8,
  output Q,
  output out_10,
  output NQ,
  output out_12,
  output out_13
);

  wire and_1_out, and_2_out, and_3_out, and_4_out, nand_1_out, nand_2_out, nand_3_out, nand_5_out,
       nand_6_out, not_1_out, not_2_out, not_3_out, not_4_out, not_5_out, or_1_out, or_2_out, or_3_out,
       or_4_out;

  not not_1 (not_1_out, set);
  not not_2 (not_2_out, CLK);
  not not_3 (not_3_out, CLK);
  nand nand_1 (nand_1_out, D, not_2_out);
  nand nand_2 (nand_2_out, nand_1_out, not_3_out);
  and and_1 (and_1_out, not_1_out, nand_1_out);
  not not_4 (not_4_out, clr);
  or or_1 (or_1_out, nand_2_out, set);
  or or_2 (or_2_out, clr, and_1_out);
  and and_2 (and_2_out, not_4_out, or_1_out);
  nand nand_3 (nand_3_out, or_2_out, out_10);
  nand nand_4 (out_10, nand_3_out, and_2_out);
  D_FF_Async d_ff_async_1 (.D(in_5), .CLK(in_6), .set(in_7), .clr(in_8), .Q(out_12), .Qn(out_13));
  nand nand_5 (nand_5_out, nand_3_out, CLK);
  nand nand_6 (nand_6_out, nand_5_out, CLK);
  and and_3 (and_3_out, not_1_out, nand_5_out);
  or or_3 (or_3_out, nand_6_out, set);
  not not_5 (not_5_out, clr);
  and and_4 (and_4_out, or_3_out, not_5_out);
  or or_4 (or_4_out, and_3_out, clr);
  nand nand_7 (NQ, Q, and_4_out);
  nand nand_8 (Q, or_4_out, NQ);
endmodule

// VHDL entity D_FF_Async, as the project stores it:
library IEEE;
use IEEE.STD_LOGIC_1164.ALL;

entity D_FF_Async is
    Port (
        D   : in  STD_LOGIC;
        CLK : in  STD_LOGIC;
        set : in  STD_LOGIC;
        clr : in  STD_LOGIC;
        Q   : out STD_LOGIC;
        Qn  : out STD_LOGIC
    );
end D_FF_Async;

architecture Behavioral of D_FF_Async is
    signal q_state : STD_LOGIC;
begin

    process(CLK, set, clr)
    begin
        if clr = '1' then
            q_state <= '0';

        elsif set = '1' then
            q_state <= '1';

        elsif rising_edge(CLK) then
            q_state <= D;

        end if;
    end process;

    Q  <= q_state;
    Qn <= not q_state;

end Behavioral;
