// Logisim project D_FlipFlop.circ as structural Verilog
module main (
  input  D,
  input  CLK,
  input  in_3,
  input  in_4,
  output Q,
  output out_6,
  output NQ,
  output out_8,
  output out_9
);

  wire nand_1_out, nand_2_out, nand_3_out, nand_5_out, nand_6_out, not_1_out;

  not not_1 (not_1_out, CLK);
  nand nand_1 (nand_1_out, D, not_1_out);
  nand nand_2 (nand_2_out, nand_1_out, not_1_out);
  nand nand_3 (nand_3_out, nand_1_out, out_6);
  nand nand_4 (out_6, nand_3_out, nand_2_out);
  D_FlipFlop d_flipflop_1 (.D(in_3), .CLK(in_4), .Q(out_8), .Qn(out_9));
  nand nand_5 (nand_5_out, nand_3_out, CLK);
  nand nand_6 (nand_6_out, nand_5_out, CLK);
  nand nand_7 (NQ, Q, nand_6_out);
  nand nand_8 (Q, nand_5_out, NQ);
endmodule

// VHDL entity D_FlipFlop, as the project stores it:
library IEEE;
use IEEE.STD_LOGIC_1164.ALL;

entity D_FlipFlop is
    Port (
        D   : in  STD_LOGIC;
        CLK : in  STD_LOGIC;
        Q   : out STD_LOGIC;
        Qn  : out STD_LOGIC
    );
end D_FlipFlop;

architecture Behavioral of D_FlipFlop is
    signal q_state : STD_LOGIC;
begin

    process(CLK)
    begin
        if rising_edge(CLK) then
            q_state <= D;
        end if;
    end process;

    Q  <= q_state;
    Qn <= not q_state;

end Behavioral;
