// Logisim project D_Latch.circ as structural Verilog
module main (
  input  D,
  input  en,
  input  in_3,
  input  in_4,
  output Q,
  output NQ,
  output out_7,
  output out_8
);

  wire nand_1_out, nand_2_out;

  nand nand_1 (nand_1_out, D, en);
  nand nand_2 (nand_2_out, nand_1_out, en);
  nand nand_3 (Q, nand_1_out, NQ);
  nand nand_4 (NQ, Q, nand_2_out);
  D_Latch d_latch_1 (.D(in_3), .en(in_4), .Q(out_7), .Qn(out_8));
endmodule

// VHDL entity D_Latch, as the project stores it:
library IEEE;
use IEEE.STD_LOGIC_1164.ALL;

entity D_Latch is
    Port (
        D   : in  STD_LOGIC;
        en  : in  STD_LOGIC;
        Q   : out STD_LOGIC;
        Qn  : out STD_LOGIC
    );
end D_Latch;

architecture Behavioral of D_Latch is
    signal q_state : STD_LOGIC;
begin

    process(D, en)
    begin
        if en = '1' then
            q_state <= D;
        end if;
    end process;

    Q  <= q_state;
    Qn <= not q_state;

end Behavioral;
