// Logisim project JK_FlipFlop.circ as structural Verilog
module main (
  input  J,
  input  K,
  input  CLK,
  input  CLR,
  input  in_5,
  input  in_6,
  input  in_7,
  output Q,
  output NQ,
  output out_10,
  output out_11
);

  wire nand_1_out, nand_2_out, nand_3_out, nand_4_out, nand_5_out, nand_6_out, not_1_out, not_2_out;

  not not_1 (not_1_out, CLR);
  not not_2 (not_2_out, CLK);
  nand nand_1 (nand_1_out, J, NQ, not_2_out);
  nand nand_2 (nand_2_out, K, Q, not_2_out);
  nand nand_3 (nand_3_out, nand_1_out, nand_4_out);
  nand nand_4 (nand_4_out, nand_3_out, not_1_out, nand_2_out);
  nand nand_5 (nand_5_out, nand_3_out, CLK);
  JK_FlipFlop jk_flipflop_1 (.J(in_5), .K(in_6), .CLK(in_7), .Q(out_10), .Qn(out_11));
  nand nand_6 (nand_6_out, nand_4_out, CLK);
  nand nand_7 (Q, nand_5_out, NQ);
  nand nand_8 (NQ, Q, not_1_out, nand_6_out);
endmodule

// VHDL entity JK_FlipFlop, as the project stores it:
library IEEE;
use IEEE.STD_LOGIC_1164.ALL;

entity JK_FlipFlop is
    Port (
        J   : in  STD_LOGIC;
        K   : in  STD_LOGIC;
        CLK : in  STD_LOGIC;
        Q   : out STD_LOGIC;
        Qn  : out STD_LOGIC
    );
end JK_FlipFlop;

architecture Behavioral of JK_FlipFlop is
    signal q_state : STD_LOGIC;
begin

    process(CLK)
    begin
        if rising_edge(CLK) then

            if J = '0' and K = '0' then
                null;                 -- Hold

            elsif J = '0' and K = '1' then
                q_state <= '0';       -- Reset

            elsif J = '1' and K = '0' then
                q_state <= '1';       -- Set

            elsif J = '1' and K = '1' then
                q_state <= not q_state; -- Toggle

            end if;

        end if;
    end process;

    Q  <= q_state;
    Qn <= not q_state;

end Behavioral;
